// Logisim project RiscV.circ as structural Verilog: 6 circuits, main circuit main
module main (
);

  wire ALUSrc, ALUzero, and_1_out, Branch, button_1_out, clock_1_out, clock_2_out, clock_3_out, MemRead,
       MemtoReg, MemWrite, not_1_out, not_2_out, RegWrite;
  wire [1:0] ALUOp;
  wire [3:0] ALUSel;
  wire [4:0] rom_1_data_2, rom_1_data_3, rom_1_data_4;
  wire [23:0] register_1_q;
  wire [31:0] adder_1_out, adder_2_out, ALUout, bancoregistradores_1_rs1, IMMext, multiplexer_1_out,
       multiplexer_2_out, multiplexer_3_out, OPCODE, RAMout, RAMrs2, rom_1_data;
  wire [31:24] register_1_q_2;

  Clock clock_1 (.out(clock_1_out));
  not not_1 (not_1_out, clock_1_out);
  ROM #(.addrWidth(24), .dataWidth(32)) rom_1 (
    .addr(register_1_q),
    .data({rom_1_data[31:25], rom_1_data_4, rom_1_data_3, rom_1_data[14:12], rom_1_data_2, rom_1_data[6:0]}));
  Multiplexer #(.width(32)) multiplexer_1 (
    .in0(adder_1_out), .in1(adder_2_out), .out(multiplexer_1_out), .sel(and_1_out));
  Register #(.width(32)) register_1 (
    .D(multiplexer_1_out), .en(not_1_out), .clk(not_1_out), .Q({register_1_q_2, register_1_q}),
    .clr(button_1_out));
  Button button_1 (.out(button_1_out));
  and and_1 (and_1_out, ALUzero, Branch);
  Adder #(.width(32)) adder_1 (.a({register_1_q_2, register_1_q}), .b(32'h4), .out(adder_1_out));  // open: cin, cout
  Adder #(.width(32)) adder_2 (.a({register_1_q_2, register_1_q}), .b(IMMext), .out(adder_2_out));  // open: cin, cout
  // Probe on RAMout
  // Probe on rom_1_data_2
  // Probe on rom_1_data_3
  // Probe on rom_1_data_4
  Multiplexer #(.width(32)) multiplexer_2 (.in0(ALUout), .in1(RAMout), .out(multiplexer_2_out), .sel(MemtoReg));
  Clock clock_2 (.out(clock_2_out));
  not not_2 (not_2_out, clock_2_out);
  // Probe on {rom_1_data[31:25], rom_1_data_4, rom_1_data_3, rom_1_data[14:12], rom_1_data_2, rom_1_data[6:0]}
  // Probe on ALUout
  // Probe on IMMext
  bancoRegistradores bancoregistradores_1 (
    .clk(not_2_out), .rsi2(rom_1_data_4), .rdi(rom_1_data_2), .data(multiplexer_2_out), .WE(RegWrite),
    .rsi1(rom_1_data_3), .rs1(bancoregistradores_1_rs1), .rs2(RAMrs2));
  ImediatoGenerator imediatogenerator_1 (
    .OPCODE({rom_1_data[31:25], rom_1_data_4, rom_1_data_3, rom_1_data[14:12], rom_1_data_2, rom_1_data[6:0]}),
    .out_2(IMMext));
  ALUCtrl aluctrl_1 (.ALUop(ALUOp), .OPCODE(OPCODE), .ALUsel(ALUSel));
  UNIDCtrl unidctrl_1 (
    .OPCODE(OPCODE), .MemWrite(MemWrite), .ALUSrc(ALUSrc), .RegWrite(RegWrite), .MemToReg(MemtoReg),
    .MemRead(MemRead), .Branch(Branch), .ALUop(ALUOp));
  // Probe on bancoregistradores_1_rs1
  // Probe on RAMrs2
  // Probe on ALUOp
  Multiplexer #(.width(32)) multiplexer_3 (.in0(RAMrs2), .in1(IMMext), .out(multiplexer_3_out), .sel(ALUSrc));
  // Probe on MemWrite
  // Probe on ALUSrc
  // Probe on MemRead
  // Probe on Branch
  // Probe on multiplexer_3_out
  // Probe on RegWrite
  // Probe on ALUSel
  ULA ula_1 (.sel(ALUSel), .dataA(bancoregistradores_1_rs1), .dataB(multiplexer_3_out), .dataD(ALUout), .zero(ALUzero));
  // Probe on MemtoReg
  // Probe on ALUout
  // Probe on ALUout[25:2]
  Clock clock_3 (.out(clock_3_out));
  // Probe on RAMrs2
  RAM #(.addrWidth(24), .dataWidth(32)) ram_1 (
    .addr(ALUout[25:2]), .we(MemWrite), .oe(MemRead), .clk(clock_3_out), .din(RAMrs2), .dout(RAMout));
  // Probe on RAMout

  // Notes on the sheet:
  //   contents of rom_1 (hex, n*v repeats v):
  //   200093
  //   endereco
endmodule

module bancoRegistradores (
  input  [4:0] rsi1,
  input  [4:0] rsi2,
  input  [4:0] rdi,
  input  [31:0] data,
  input  WE,
  input  clk,
  output [31:0] rs1,
  output [31:0] rs2
);

  wire x0we_t, x1we_t, x2we_t, x3we_t, x4we_t, x5we_t, x6we_t, x7we_t, x8we_t, x9we_t, x10we_t, x11we_t,
       x12we_t, x13we_t, x14we_t, x15we_t, x16we_t, x17we_t, x18we_t, x19we_t, x20we_t, x21we_t, x22we_t,
       x23we_t, x24we_t, x25we_t, x26we_t, x27we_t, x28we_t, x29we_t, x30we_t, x31we_t;
  wire [31:0] x1q_t, x2q_t, x3q_t, x4q_t, x5q_t, x6q_t, x7q_t, x8q_t, x9q_t, x10q_t, x11q_t, x12q_t, x13q_t,
       x14q_t, x15q_t, x16q_t, x17q_t, x18q_t, x19q_t, x20q_t, x21q_t, x22q_t, x23q_t, x24q_t, x25q_t,
       x26q_t, x27q_t, x28q_t, x29q_t, x30q_t, x31q_t;

  Demultiplexer #(.select(5)) demultiplexer_1 (
    .out0(x0we_t), .out1(x1we_t), .out2(x2we_t), .out3(x3we_t), .out4(x4we_t), .out5(x5we_t), .out6(x6we_t),
    .out7(x7we_t), .out8(x8we_t), .out9(x9we_t), .out10(x10we_t), .out11(x11we_t), .out12(x12we_t),
    .out13(x13we_t), .out14(x14we_t), .out15(x15we_t), .out16(x16we_t), .out17(x17we_t), .out18(x18we_t),
    .out19(x19we_t), .out20(x20we_t), .out21(x21we_t), .out22(x22we_t), .out23(x23we_t), .out24(x24we_t),
    .out25(x25we_t), .out26(x26we_t), .out27(x27we_t), .out28(x28we_t), .out29(x29we_t), .out30(x30we_t),
    .out31(x31we_t), .in(WE), .sel(rdi));
  Register #(.width(32)) x4 (.D(data), .en(x4we_t), .clk(clk), .Q(x4q_t));  // open: clr
  Register #(.width(32)) x8 (.D(data), .en(x8we_t), .clk(clk), .Q(x8q_t));  // open: clr
  Register #(.width(32)) x12 (.D(data), .en(x12we_t), .clk(clk), .Q(x12q_t));  // open: clr
  Register #(.width(32)) x16 (.D(data), .en(x16we_t), .clk(clk), .Q(x16q_t));  // open: clr
  Register #(.width(32)) x20 (.D(data), .en(x20we_t), .clk(clk), .Q(x20q_t));  // open: clr
  Register #(.width(32)) x24 (.D(data), .en(x24we_t), .clk(clk), .Q(x24q_t));  // open: clr
  Register #(.width(32)) x28 (.D(data), .en(x28we_t), .clk(clk), .Q(x28q_t));  // open: clr
  Register #(.width(32)) x1 (.D(data), .en(x1we_t), .clk(clk), .Q(x1q_t));  // open: clr
  Register #(.width(32)) x5 (.D(data), .en(x5we_t), .clk(clk), .Q(x5q_t));  // open: clr
  Register #(.width(32)) x9 (.D(data), .en(x9we_t), .clk(clk), .Q(x9q_t));  // open: clr
  Register #(.width(32)) x13 (.D(data), .en(x13we_t), .clk(clk), .Q(x13q_t));  // open: clr
  Register #(.width(32)) x17 (.D(data), .en(x17we_t), .clk(clk), .Q(x17q_t));  // open: clr
  Register #(.width(32)) x21 (.D(data), .en(x21we_t), .clk(clk), .Q(x21q_t));  // open: clr
  Register #(.width(32)) x25 (.D(data), .en(x25we_t), .clk(clk), .Q(x25q_t));  // open: clr
  Register #(.width(32)) x29 (.D(data), .en(x29we_t), .clk(clk), .Q(x29q_t));  // open: clr
  Register #(.width(32)) x2 (.D(data), .en(x2we_t), .clk(clk), .Q(x2q_t));  // open: clr
  Register #(.width(32)) x6 (.D(data), .en(x6we_t), .clk(clk), .Q(x6q_t));  // open: clr
  Register #(.width(32)) x10 (.D(data), .en(x10we_t), .clk(clk), .Q(x10q_t));  // open: clr
  Register #(.width(32)) x14 (.D(data), .en(x14we_t), .clk(clk), .Q(x14q_t));  // open: clr
  Register #(.width(32)) x18 (.D(data), .en(x18we_t), .clk(clk), .Q(x18q_t));  // open: clr
  Register #(.width(32)) x22 (.D(data), .en(x22we_t), .clk(clk), .Q(x22q_t));  // open: clr
  Register #(.width(32)) x26 (.D(data), .en(x26we_t), .clk(clk), .Q(x26q_t));  // open: clr
  Register #(.width(32)) x30 (.D(data), .en(x30we_t), .clk(clk), .Q(x30q_t));  // open: clr
  Register #(.width(32)) x3 (.D(data), .en(x3we_t), .clk(clk), .Q(x3q_t));  // open: clr
  Register #(.width(32)) x7 (.D(data), .en(x7we_t), .clk(clk), .Q(x7q_t));  // open: clr
  Register #(.width(32)) x11 (.D(data), .en(x11we_t), .clk(clk), .Q(x11q_t));  // open: clr
  Register #(.width(32)) x15 (.D(data), .en(x15we_t), .clk(clk), .Q(x15q_t));  // open: clr
  Register #(.width(32)) x19 (.D(data), .en(x19we_t), .clk(clk), .Q(x19q_t));  // open: clr
  Register #(.width(32)) x23 (.D(data), .en(x23we_t), .clk(clk), .Q(x23q_t));  // open: clr
  Register #(.width(32)) x27 (.D(data), .en(x27we_t), .clk(clk), .Q(x27q_t));  // open: clr
  Register #(.width(32)) x31 (.D(data), .en(x31we_t), .clk(clk), .Q(x31q_t));  // open: clr
  Multiplexer #(.select(5), .width(32)) multiplexer_1 (
    .in0({32{1'b0}}), .in1(x1q_t), .in2(x2q_t), .in3(x3q_t), .in4(x4q_t), .in5(x5q_t), .in6(x6q_t),
    .in7(x7q_t), .in8(x8q_t), .in9(x9q_t), .in10(x10q_t), .in11(x11q_t), .in12(x12q_t), .in13(x13q_t),
    .in14(x14q_t), .in15(x15q_t), .in16(x16q_t), .in17(x17q_t), .in18(x18q_t), .in19(x19q_t), .in20(x20q_t),
    .in21(x21q_t), .in22(x22q_t), .in23(x23q_t), .in24(x24q_t), .in25(x25q_t), .in26(x26q_t), .in27(x27q_t),
    .in28(x28q_t), .in29(x29q_t), .in30(x30q_t), .in31(x31q_t), .out(rs1), .sel(rsi1));
  Multiplexer #(.select(5), .width(32)) multiplexer_2 (
    .in0({32{1'b0}}), .in1(x1q_t), .in2(x2q_t), .in3(x3q_t), .in4(x4q_t), .in5(x5q_t), .in6(x6q_t),
    .in7(x7q_t), .in8(x8q_t), .in9(x9q_t), .in10(x10q_t), .in11(x11q_t), .in12(x12q_t), .in13(x13q_t),
    .in14(x14q_t), .in15(x15q_t), .in16(x16q_t), .in17(x17q_t), .in18(x18q_t), .in19(x19q_t), .in20(x20q_t),
    .in21(x21q_t), .in22(x22q_t), .in23(x23q_t), .in24(x24q_t), .in25(x25q_t), .in26(x26q_t), .in27(x27q_t),
    .in28(x28q_t), .in29(x29q_t), .in30(x30q_t), .in31(x31q_t), .out(rs2), .sel(rsi2));

  // Other names for the same wires on the sheet: clk_t = clk; rd_t[31:0] = data; rdi_t[4:0] = rdi; rs1_t[31:0] = rs1;
  //   rs2_t[31:0] = rs2; rsi1_t[4:0] = rsi1; rsi2_t[4:0] = rsi2; we_t = WE
endmodule

module ULA (
  input  [31:0] dataA,
  input  [31:0] dataB,
  input  [3:0] sel,
  output [31:0] dataD,
  output zero
);

  wire [31:0] adder_1_out, and_1_out, or_1_out, shifter_1_out, subtractor_1_out;

  // Probe on and_1_out
  assign and_1_out = dataA & dataB;  // AND_Gate and_1, 32 bits wide
  // Probe on or_1_out
  assign or_1_out = dataA | dataB;  // OR_Gate or_1, 32 bits wide
  // Probe on adder_1_out
  Adder #(.width(32)) adder_1 (.a(dataA), .b(dataB), .out(adder_1_out));  // open: cin, cout
  // Probe on shifter_1_out
  Shifter #(.width(32)) shifter_1 (.in(dataA), .\dist (dataB[4:0]), .out(shifter_1_out));
  Subtractor #(.width(32)) subtractor_1 (.a(dataA), .b(dataB), .out(subtractor_1_out));  // open: bin, bout
  // Probe on subtractor_1_out
  Multiplexer #(.select(4), .width(32)) multiplexer_1 (
    .in0(and_1_out), .in1(or_1_out), .in2(adder_1_out), .in3(shifter_1_out), .in4(dataB), .in5(dataB),
    .in6(subtractor_1_out), .in7(dataB), .in8(dataB), .in9(dataB), .in10(dataB), .in11(dataB), .in12(dataB),
    .in13(dataB), .in14(dataB), .in15(dataB), .out(dataD), .sel(sel));
  nor nor_1 (zero, dataD[0], dataD[1], dataD[2], dataD[3], dataD[4], dataD[5], dataD[6], dataD[7], dataD[8], dataD[9], dataD[10], dataD[11], dataD[12], dataD[13], dataD[14], dataD[15], dataD[16], dataD[17], dataD[18], dataD[19], dataD[20], dataD[21], dataD[22], dataD[23], dataD[24], dataD[25], dataD[26], dataD[27], dataD[28], dataD[29], dataD[30], dataD[31]);

  // Other names for the same wires on the sheet: dataA_t[31:0] = dataA; dataB_t[31:0] = dataB; dataD_t[31:0] = dataD;
  //   sel_t[3:0] = sel

  // Notes on the sheet:
  //   desloca no maximo 2 elevado a 5 menos 1
  //   0000 and
  //   0001 or
  //   0010 add
  //   0110 sub
  //   0011 sll
  //   depois implementos o restante
endmodule

module ImediatoGenerator (
  input  [31:0] OPCODE,
  output [31:0] out_2
);

  wire and_1_out, and_2_out, and_3_out, and_5_out, and_6_out, S0, S1, S2;
  wire [31:0] bit_extender_1_out, bit_extender_2_out, bit_extender_3_out, bit_extender_4_out;

  // Probe on OPCODE[6:0]
  and and_1 (and_1_out, OPCODE[0], OPCODE[1], OPCODE[2], ~OPCODE[4], OPCODE[5], OPCODE[6]);  // AND_Gate
  and and_2 (and_2_out, OPCODE[0], OPCODE[1], ~OPCODE[2], ~OPCODE[3], OPCODE[5], OPCODE[6]);  // AND_Gate
  and and_3 (and_3_out, OPCODE[0], OPCODE[1], ~OPCODE[2], ~OPCODE[3], ~OPCODE[5], ~OPCODE[6]);  // AND_Gate
  and and_4 (S1, OPCODE[0], OPCODE[1], ~OPCODE[2], ~OPCODE[4], ~OPCODE[3], OPCODE[5]);  // AND_Gate
  and and_5 (and_5_out, OPCODE[0], OPCODE[1], OPCODE[2], OPCODE[3], ~OPCODE[4], OPCODE[5], OPCODE[6]);  // AND_Gate
  and and_6 (and_6_out, OPCODE[0], OPCODE[1], OPCODE[2], ~OPCODE[3], OPCODE[4], OPCODE[5], ~OPCODE[6]);  // AND_Gate
  or or_1 (S2, and_1_out, and_2_out, and_3_out);
  or or_2 (S0, and_5_out, and_6_out);
  // Probe on {S0, S1, S2}
  assign bit_extender_1_out = {{20{OPCODE[31]}}, OPCODE[31:20]};  // Bit_Extender bit_extender_1
  // Probe on bit_extender_1_out
  assign bit_extender_2_out = {{20{OPCODE[31]}}, {OPCODE[31:25], OPCODE[11:7]}};  // Bit_Extender bit_extender_2
  assign bit_extender_3_out = {{19{OPCODE[31]}}, {OPCODE[31], OPCODE[7], OPCODE[30:25], OPCODE[11:8], 1'b0}};  // Bit_Extender bit_extender_3
  // Probe on bit_extender_3_out
  // Probe on {OPCODE[31:12], {12{1'b0}}}
  // Probe on bit_extender_2_out
  // Probe on {OPCODE[31], OPCODE[19:12], OPCODE[20], OPCODE[30:21], 1'b0}
  assign bit_extender_4_out = {{11{OPCODE[31]}}, {OPCODE[31], OPCODE[19:12], OPCODE[20], OPCODE[30:21], 1'b0}};  // Bit_Extender bit_extender_4
  Multiplexer #(.select(3), .width(32)) multiplexer_1 (
    .in1(bit_extender_1_out), .in2(bit_extender_2_out), .in3(bit_extender_3_out),
    .in4({OPCODE[31:12], {12{1'b0}}}), .in5(bit_extender_4_out), .out(out_2), .sel({S0, S1, S2}));  // open: in0, in6, in7
  // Probe on out_2

  // Other names for the same wires on the sheet: A = OPCODE[0]; B = OPCODE[1]; C = OPCODE[2]; D = OPCODE[3];
  //   E = OPCODE[4]; F = OPCODE[5]; G = OPCODE[6]; seletor[2:0] = {S0, S1, S2}

  // Notes on the sheet:
  //   OPCODE: initial=0x7a17d
  //   separa os bits em um circ combinacional e gera 3 bits de controle para o mux dependendo do OPCODE
  //   tipo S
  //   tipo U
  //   tipo J
  //   tipo I
  //   tipo B
endmodule

module ALUCtrl (
  input  [1:0] ALUop,
  input  [31:0] OPCODE,
  output [3:0] ALUsel
);

  wire and_1_out, and_2_out, and_3_out, or_1_out;

  and and_1 (and_1_out, OPCODE[14], OPCODE[13], ~OPCODE[12]);  // AND_Gate
  and and_2 (and_2_out, ~OPCODE[14], ~OPCODE[13], OPCODE[12]);  // AND_Gate
  and and_3 (and_3_out, ALUop[1], OPCODE[30], ~OPCODE[14], ~OPCODE[13], ~OPCODE[12]);  // AND_Gate
  or or_1 (or_1_out, and_1_out, and_2_out);
  or or_2 (ALUsel[1], ~ALUop[1], ALUop[0], ~OPCODE[14], ~OPCODE[13]);  // OR_Gate
  or or_3 (ALUsel[2], ALUop[0], and_3_out);
  // NoConnect on nothing
  and and_4 (ALUsel[0], ALUop[1], ~ALUop[0], or_1_out);  // AND_Gate

  assign ALUsel[3] = 1'b0;

  // Other names for the same wires on the sheet: A0 = ALUop[0]; A1 = ALUop[1]; F0 = OPCODE[12]; F1 = OPCODE[13];
  //   F2 = OPCODE[14]; F7 = OPCODE[30]

  // Notes on the sheet:
  //   ALUop
  //   funct3
  //   funct7
  //   A1 · ~A0 · ( (F2 · F1 · ~F0) + (~F2 · ~F1 · F0) )
  //   (~A1 + A0 + ~F2 + ~F1)
  //   A0 + (A1 · F7 · ~F2 · ~F1 · ~F0)
endmodule

module UNIDCtrl (
  input  [31:0] OPCODE,
  output MemWrite,
  output ALUSrc,
  output RegWrite,
  output MemToReg,
  output MemRead,
  output Branch,
  output [1:0] ALUop
);

  wire and_2_out;

  and and_1 (MemWrite, ~OPCODE[4], OPCODE[5], ~OPCODE[6]);  // AND_Gate
  and and_2 (and_2_out, ~OPCODE[5], ~OPCODE[6]);  // AND_Gate
  and and_3 (MemRead, ~OPCODE[4], ~OPCODE[5], ~OPCODE[6]);  // AND_Gate
  and and_4 (ALUop[1], OPCODE[4], OPCODE[5], ~OPCODE[6]);  // AND_Gate
  and and_5 (ALUop[0], ~OPCODE[4], OPCODE[5], OPCODE[6]);  // AND_Gate
  or or_1 (ALUSrc, MemWrite, and_2_out);
  or or_2 (RegWrite, and_2_out, ALUop[1]);

  assign Branch = ALUop[0];
  assign MemToReg = MemRead;

  // Other names for the same wires on the sheet: op_4 = OPCODE[4]; op_5 = OPCODE[5]; op_6 = OPCODE[6]
endmodule
