// Digital circuit Banco de Registradores.dig as structural Verilog
module Banco_de_Registradores (
  input  rd_0,
  input  rd_1,
  input  rd_2,
  input  rd_3,
  input  rd_4,
  input  rd_5,
  input  rd_6,
  input  rd_7,
  input  enable,
  input  clk,
  input  FE0,
  input  FE1,
  input  Rs1_B0,
  input  Rs1_B1,
  input  Rs2_B0,
  input  Rs2_B1,
  output Rs1_S0,
  output Rs2_S0,
  output Rs1_S1,
  output Rs1_S2,
  output Rs1_S3,
  output Rs1_S4,
  output Rs1_S5,
  output Rs1_S6,
  output Rs1_S7,
  output Rs2_S1,
  output Rs2_S2,
  output Rs2_S3,
  output Rs2_S4,
  output Rs2_S5,
  output Rs2_S6,
  output Rs2_S7
);

  wire escolha_reg_b1, escolha_reg_b2, escolha_reg_b3, Reg1_out_0, Reg1_out_1, Reg1_out_2, Reg1_out_3,
       Reg1_out_4, Reg1_out_5, Reg1_out_6, Reg1_out_7, Reg2_out_0, Reg2_out_1, Reg2_out_2, Reg2_out_3,
       Reg2_out_4, Reg2_out_5, Reg2_out_6, Reg2_out_7, reg3_out_0, reg3_out_1, reg3_out_2, reg3_out_3,
       reg3_out_4, reg3_out_5, reg3_out_6, reg3_out_7;

  Demux_1x4 escolha_reg (
    .Enable(enable), .B1(escolha_reg_b1), .B2(escolha_reg_b2), .B3(escolha_reg_b3), .S1(FE1), .S0(FE0));  // open: B0
  Registrador Reg1 (
    .in_0(rd_0), .in_1(rd_1), .in_2(rd_2), .in_3(rd_3), .in_4(rd_4), .in_5(rd_5), .in_6(rd_6), .in_7(rd_7),
    .clk(clk), .Enable(escolha_reg_b1), .out_0(Reg1_out_0), .out_1(Reg1_out_1), .out_2(Reg1_out_2),
    .out_3(Reg1_out_3), .out_4(Reg1_out_4), .out_5(Reg1_out_5), .out_6(Reg1_out_6), .out_7(Reg1_out_7));
  Registrador Reg2 (
    .in_0(rd_0), .in_1(rd_1), .in_2(rd_2), .in_3(rd_3), .in_4(rd_4), .in_5(rd_5), .in_6(rd_6), .in_7(rd_7),
    .clk(clk), .Enable(escolha_reg_b2), .out_0(Reg2_out_0), .out_1(Reg2_out_1), .out_2(Reg2_out_2),
    .out_3(Reg2_out_3), .out_4(Reg2_out_4), .out_5(Reg2_out_5), .out_6(Reg2_out_6), .out_7(Reg2_out_7));
  Registrador reg3 (
    .in_0(rd_0), .in_1(rd_1), .in_2(rd_2), .in_3(rd_3), .in_4(rd_4), .in_5(rd_5), .in_6(rd_6), .in_7(rd_7),
    .clk(clk), .Enable(escolha_reg_b3), .out_0(reg3_out_0), .out_1(reg3_out_1), .out_2(reg3_out_2),
    .out_3(reg3_out_3), .out_4(reg3_out_4), .out_5(reg3_out_5), .out_6(reg3_out_6), .out_7(reg3_out_7));
  mux8bits_4x1 Rgs_1 (
    .In_A0(1'b0), .In_A1(1'b0), .In_A2(1'b0), .In_A3(1'b0), .In_A4(1'b0), .In_A5(1'b0), .In_A6(1'b0),
    .In_A7(1'b0), .In_B0(Reg1_out_0), .In_B1(Reg1_out_1), .In_B2(Reg1_out_2), .In_B3(Reg1_out_3),
    .In_B4(Reg1_out_4), .In_B5(Reg1_out_5), .In_B6(Reg1_out_6), .In_B7(Reg1_out_7), .In_C0(Reg2_out_0),
    .In_C1(Reg2_out_1), .In_C2(Reg2_out_2), .In_C3(Reg2_out_3), .In_C4(Reg2_out_4), .In_C5(Reg2_out_5),
    .In_C6(Reg2_out_6), .In_C7(Reg2_out_7), .In_D0(reg3_out_0), .In_D1(reg3_out_1), .In_D2(reg3_out_2),
    .In_D3(reg3_out_3), .In_D4(reg3_out_4), .In_D5(reg3_out_5), .In_D6(reg3_out_6), .In_D7(reg3_out_7),
    .F1(Rs1_B1), .F0(Rs1_B0), .S0(Rs1_S0), .S1(Rs1_S1), .S2(Rs1_S2), .S3(Rs1_S3), .S4(Rs1_S4), .S5(Rs1_S5),
    .S6(Rs1_S6), .S7(Rs1_S7));
  mux8bits_4x1 Rgs_2 (
    .In_A0(1'b0), .In_A1(1'b0), .In_A2(1'b0), .In_A3(1'b0), .In_A4(1'b0), .In_A5(1'b0), .In_A6(1'b0),
    .In_A7(1'b0), .In_B0(Reg1_out_0), .In_B1(Reg1_out_1), .In_B2(Reg1_out_2), .In_B3(Reg1_out_3),
    .In_B4(Reg1_out_4), .In_B5(Reg1_out_5), .In_B6(Reg1_out_6), .In_B7(Reg1_out_7), .In_C0(Reg2_out_0),
    .In_C1(Reg2_out_1), .In_C2(Reg2_out_2), .In_C3(Reg2_out_3), .In_C4(Reg2_out_4), .In_C5(Reg2_out_5),
    .In_C6(Reg2_out_6), .In_C7(Reg2_out_7), .In_D0(reg3_out_0), .In_D1(reg3_out_1), .In_D2(reg3_out_2),
    .In_D3(reg3_out_3), .In_D4(reg3_out_4), .In_D5(reg3_out_5), .In_D6(reg3_out_6), .In_D7(reg3_out_7),
    .F1(Rs2_B1), .F0(Rs2_B0), .S0(Rs2_S0), .S1(Rs2_S1), .S2(Rs2_S2), .S3(Rs2_S3), .S4(Rs2_S4), .S5(Rs2_S5),
    .S6(Rs2_S6), .S7(Rs2_S7));
endmodule
